// Logisim project b1.circ as structural Verilog: 6 circuits, main circuit main
module main (
  input  A,
  input  B,
  input  C,
  output out_4
);

  wire not_1_out, or_1_out, undriven;

  or or_1 (or_1_out, A, B);
  not not_1 (not_1_out, or_1_out);
  or or_2 (out_4, not_1_out, undriven);

  // Notes on the sheet:
  //   A+B
  //   -(A+B)
  //   -(A+B)+C
endmodule

module \bài_2  (
  input  A,
  input  B,
  input  C,
  output out_4
);

  wire not_1_out, or_1_out, or_2_out;

  or or_1 (or_1_out, A, B);
  not not_1 (not_1_out, A);
  or or_2 (or_2_out, not_1_out, C);
  and and_1 (out_4, or_1_out, or_2_out);

  // Notes on the sheet:
  //   A+B
  //   -A
  //   -A+C
  //   (A+B)(-A+C)
endmodule

module bai3 (
  input  A,
  input  B,
  input  C,
  output out_4
);

  wire not_1_out, not_2_out, or_1_out;

  not not_1 (not_1_out, A);
  not not_2 (not_2_out, C);
  or or_1 (or_1_out, not_1_out, B);
  and and_1 (out_4, or_1_out, not_2_out);

  // Notes on the sheet:
  //   -A+B
  //   (-A+B)C
endmodule

module bai_4 (
  input  A,
  input  B,
  input  C,
  output out_4
);

  wire and_1_out, not_1_out, not_2_out, not_3_out;

  not not_1 (not_1_out, A);
  and and_1 (and_1_out, not_1_out, B);
  not not_2 (not_2_out, C);
  not not_3 (not_3_out, and_1_out);
  or or_1 (out_4, A, not_3_out, not_2_out);

  // Notes on the sheet:
  //   -A
  //   -AB
  //   -(-AB)
  //   -C
  //   -(-AB) + A +(-C)
endmodule

module bai5 (
  input  A,
  input  B,
  input  C,
  output out_4
);

  wire and_1_out, and_2_out, not_1_out;

  and and_1 (and_1_out, A, B);
  and and_2 (and_2_out, B, C);
  not not_1 (not_1_out, and_1_out);
  or or_1 (out_4, not_1_out, and_2_out);

  // Notes on the sheet:
  //   AB
  //   BC
  //   -(AB)
  //   -(AB)+BC
endmodule

module bai6 (
  input  A,
  input  B,
  input  D,
  output A_B__XOR__B_D
);

  wire not_1_out, or_1_out, or_2_out;

  or or_1 (or_1_out, A, B);
  or or_2 (or_2_out, B, D);
  not not_1 (not_1_out, or_1_out);
  xor xor_1 (A_B__XOR__B_D, not_1_out, or_2_out);

  // Notes on the sheet:
  //   A+B
  //   B+D
  //   -(A+B)
endmodule
