// Logisim project b2.circ as structural Verilog
module main (
  input  A,
  input  B,
  input  C,
  output out_4
);

  wire nor_1_out, nor_2_out;

  nor nor_1 (nor_1_out, A, B);
  nor nor_2 (nor_2_out, nor_1_out, C);
  not not_1 (out_4, nor_2_out);
endmodule

module bai2 (
  input  A,
  input  B,
  input  C,
  output out_4
);

  wire nor_1_out, nor_2_out, not_1_out;

  nor nor_1 (nor_1_out, A, B);
  not not_1 (not_1_out, A);
  nor nor_2 (nor_2_out, not_1_out, C);
  nor nor_3 (out_4, nor_1_out, nor_1_out, nor_2_out);
endmodule

module bai3 (
  input  A,
  input  B,
  input  C,
  output out_4
);

  wire not_1_out, xor_1_out;

  not not_1 (not_1_out, A);
  xor xor_1 (xor_1_out, not_1_out, B);
  xor xor_2 (out_4, xor_1_out, C);
endmodule

module bai4 (
  input  A,
  input  B,
  input  C,
  output out_4
);

  wire nor_1_out, nor_2_out, not_1_out, not_2_out, not_3_out;

  not not_1 (not_1_out, A);
  not not_2 (not_2_out, C);
  nor nor_1 (nor_1_out, not_1_out, B);
  nor nor_2 (nor_2_out, A, not_2_out);
  not not_3 (not_3_out, nor_1_out);
  nand nand_1 (out_4, not_3_out, nor_2_out);
endmodule

module bai5 (
  input  A,
  input  B,
  input  C,
  output out_4
);

  wire nand_1_out, nor_1_out, nor_2_out, not_1_out, not_2_out;

  not not_1 (not_1_out, B);
  not not_2 (not_2_out, C);
  nand nand_1 (nand_1_out, A, B);
  nor nor_1 (nor_1_out, not_1_out, not_2_out);
  nor nor_2 (nor_2_out, nand_1_out, nor_1_out);
  not not_3 (out_4, nor_2_out);
endmodule
